# Fritzing sketch Kaffee-Counter (saved by Fritzing 1.0.2b)

parts:
  LCM1602_IIC1 = LCM1602 IIC [part_number="LCM1602 IIC" chip_label="LCM1602 IIC" package="DIP (Dual Inline) [THT]"]
  Mod2 = Raspberry Pi Pico W
  Bauteil1 = RFID-RC522-v2
  Bauteil2 = Adafruit DS1307 RTC Breakout [part_number="Adafruit #264"]
  U2 = WS2812 RGB LED strip
  SP1 = SPEAKER [package=pcb_mount_speaker]
  U1 = LCD-16X2 [package=lcd-16x2]

nets:
  VSS: LCM1602_IIC1.VSS, U1.VSS
  VDD: LCM1602_IIC1.VDD, U1.VDD
  N1: LCM1602_IIC1.V0, U1.VO
  N2: LCM1602_IIC1.RS, U1.RS
  N3: LCM1602_IIC1.RW, U1.R_W
  N4: LCM1602_IIC1.E, U1.E
  N5: LCM1602_IIC1.D0, U1.DB0
  N6: LCM1602_IIC1.D1, U1.DB1
  N7: LCM1602_IIC1.D2, U1.DB2
  N8: LCM1602_IIC1.D3, U1.DB3
  N9: LCM1602_IIC1.D4, U1.DB4
  N10: LCM1602_IIC1.D5, U1.DB5
  N11: LCM1602_IIC1.D6, U1.DB6
  N12: LCM1602_IIC1.D7, U1.DB7
  N13: LCM1602_IIC1.A, U1.A
  N14: LCM1602_IIC1.K, U1.K
  GND: LCM1602_IIC1.GND, Mod2.pin_3, Mod2.pin_18, Mod2.pin_33, Mod2.pin_38, Bauteil1.GND, Bauteil2.GND, U2.GND, SP1.+
  VCC: LCM1602_IIC1.VCC, Mod2.pin_39, U2.VCC
  N15: LCM1602_IIC1.SDA, Mod2.pin_19
  N16: LCM1602_IIC1.SCL, Mod2.pin_20
  N17: LCM1602_IIC1.LED_A, LCM1602_IIC1.LED_B
  N18: Mod2.pin_6, Bauteil1.MISO
  N19: Mod2.pin_7, Bauteil1.SDA
  N20: Mod2.pin_9, Bauteil1.SCK
  N21: Mod2.pin_10, Bauteil1.MOSI
  N22: Mod2.pin_15, U2.DIN
  N23: Mod2.pin_17, SP1.-
  N24: Mod2.pin_21, Bauteil2.SDA
  N25: Mod2.pin_22, Bauteil2.SCL
  N26: Mod2.pin_29, Bauteil1.RST
  N27: Mod2.pin_36, Bauteil1.3.3V

custom parts:
  LCM1602 IIC: I2C-Module to use a 1602 or 2004 LCD on with the wire.h libory Serial LCD Modul
  Raspberry Pi Pico W: Raspberry Pi Pico W. Based around the RP2040 microcontroller the Pico W is a low cost microcontroller device bringing Raspberry Pi quality, cost, and easy of use to the microcontroller space. The areas marked KEEPOUT in pcb silkscreen should not have traces running through them to avoid shorts on a soldered in module!
  RFID-RC522-v2: A simple China made RFID-RC522 Reader; do check the pin labels, as this is a MFRC522 based clone.
  Adafruit DS1307 RTC Breakout: This is a great battery-backed real time clock (RTC) that allows your microcontroller project to keep track of time even if it is reprogrammed, or if the power is lost. Perfect for datalogging, clock-building, time stamping, timers and alarms, etc. The DS1307 is the most popular RTC - but it requires 5V power to work (although we've used it with 5V power and 3.3V logic successfully) PCB &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
  WS2812 RGB LED strip: WS2812 strip
